# Fritzing sketch Semaforo (saved by Fritzing 0.9.3b)
breadboards: 1

parts:
  R1 = Rotary Potentiometer (Small) [maximum_resistance=100kΩ package=THT]
  LED1 = LED - 5mm [color="Red (633nm)" package="5 mm [THT]"]
  LED2 = LED - 5mm [color="Yellow (595nm)" package="5 mm [THT]"]
  LED3 = LED - 5mm [color="Green (565nm)" package="5 mm [THT]"]
  LED5 = LED - 5mm [color="Red (633nm)" package="5 mm [THT]"]
  LED6 = LED - 5mm [color="Green (565nm)" package="5 mm [THT]"]
  S1 = Pushbutton [package="[THT]"]
  Componente1 = Arduino Uno (Rev3)
  R2 = Resistor [tolerance=±5% resistance=220 package=THT]
  R3 = Resistor [tolerance=±5% resistance=220 package=THT]
  R4 = Resistor [tolerance=±5% resistance=220 package=THT]
  R5 = Resistor [tolerance=±5% resistance=220 package=THT]
  R6 = Resistor [tolerance=±5% resistance=220 package=THT]

nets:
  N1: R1.leg1, S1.Pin_3, S1.Pin_4
  N2: R1.wiper, Componente1.A0
  N3: R1.leg2, R2.Pin_0, R3.Pin_0, R4.Pin_0, R5.Pin_0, R6.Pin_0
  N4: LED1.cathode, R2.Pin_1
  N5: LED1.anode, Componente1.D7
  N6: LED2.cathode, R3.Pin_1
  N7: LED2.anode, Componente1.D6_PWM
  N8: LED3.cathode, R4.Pin_1
  N9: LED3.anode, Componente1.D5_PWM
  N10: LED5.cathode, R6.Pin_1
  N11: LED5.anode, Componente1.D2
  N12: LED6.cathode, R5.Pin_1
  N13: LED6.anode, Componente1.D4
  N14: S1.Pin_1, S1.Pin_2, Componente1.D8
